# Fritzing sketch circuit (saved by Fritzing 0.9.3b)

parts:
  S1 = Round Pushbutton
  LED1 = smd LED [color="Red (633nm)" package="0805 [SMD]"]
  VCC1 = Battery

nets:
  N1: S1.leg0, LED1.cathode
  N2: S1.leg1, VCC1.-
